// Logisim project Gets_IC.circ as structural Verilog: 9 circuits, main circuit IC7432 (OR)
// OR
module IC7432__OR (
  input  _1,
  input  _14_VCC,
  input  _2,
  input  _13,
  input  _12,
  input  _4,
  input  _5,
  input  _10,
  input  _9,
  input  _7_GND,
  output _3,
  output _11,
  output _6,
  output _8
);

  or or_1 (_3, _2, _1);
  or or_2 (_6, _5, _4);
  or or_3 (_11, _13, _12);
  or or_4 (_8, _10, _9);
endmodule

// AND
module IC7408__AND (
  input  _1,
  input  _14_VCC,
  input  _2,
  input  _13,
  input  _12,
  input  _4,
  input  _5,
  input  _10,
  input  _9,
  input  _7_GND,
  output _3,
  output _11,
  output _6,
  output _8
);

  and and_1 (_3, _2, _1);
  and and_2 (_6, _5, _4);
  and and_3 (_11, _13, _12);
  and and_4 (_8, _10, _9);
endmodule

// NOT
module IC7404__NOT (
  input  _1,
  input  _14_VCC,
  input  _13,
  input  _3,
  input  _10,
  input  _5,
  input  _9,
  input  _7_GND,
  output _2,
  output _12,
  output _3_2,
  output _11,
  output _6,
  output _8
);

  not not_1 (_2, _1);
  not not_2 (_3_2, _3);
  not not_3 (_6, _5);
  not not_4 (_12, _13);
  not not_5 (_11, _10);
  not not_6 (_8, _9);
endmodule

// NAND
module IC7400__NAND (
  input  _1,
  input  _14_VCC,
  input  _2,
  input  _13,
  input  _12,
  input  _4,
  input  _5,
  input  _10,
  input  _9,
  input  _7_GND,
  output _3,
  output _11,
  output _6,
  output _8
);

  nand nand_1 (_3, _2, _1);
  nand nand_2 (_6, _5, _4);
  nand nand_3 (_11, _13, _12);
  nand nand_4 (_8, _10, _9);
endmodule

// NOR
module IC7402__NOR (
  input  _14_VCC,
  input  _2,
  input  _3,
  input  _12,
  input  _11,
  input  _5,
  input  _6,
  input  _9,
  input  _7_GND,
  input  _8,
  output _1,
  output _13,
  output _4,
  output _10
);

  nor nor_1 (_1, _2, _3);
  nor nor_2 (_4, _5, _6);
  nor nor_3 (_13, _11, _12);
  nor nor_4 (_10, _8, _9);
endmodule

// XOR
module IC7486__X_OR (
  input  _1,
  input  _14_VCC,
  input  _2,
  input  _13,
  input  _12,
  input  _4,
  input  _5,
  input  _10,
  input  _9,
  input  _7_GND,
  output _3,
  output _11,
  output _6,
  output _8
);

  xor xor_1 (_3, _2, _1);
  xor xor_2 (_6, _5, _4);
  xor xor_3 (_11, _13, _12);
  xor xor_4 (_8, _10, _9);
endmodule

module IC74266__X_NOR (
  input  _1,
  input  _14_VCC,
  input  _2,
  input  _13,
  input  _12,
  input  _5,
  input  _4,
  input  _9,
  input  _7_GND,
  input  _10,
  output _3,
  output _6,
  output _11,
  output _8
);

  xnor xnor_1 (_3, _2, _1);
  xnor xnor_2 (_6, _5, _4);
  xnor xnor_3 (_11, _13, _12);
  xnor xnor_4 (_8, _10, _9);
endmodule

module IC7411__AND_3 (
  input  _1,
  input  _14_VCC,
  input  _2,
  input  _13,
  input  _3,
  input  _4,
  input  _11,
  input  _5,
  input  _10,
  input  _9,
  input  _7_GND,
  output _12,
  output _6,
  output _8
);

  and and_1 (_6, _5, _4, _3);
  and and_2 (_12, _2, _1, _13);
  and and_3 (_8, _11, _10, _9);
endmodule

module IC4075__OR_3 (
  input  _1,
  input  _14_VCC,
  input  _2,
  input  _13,
  input  _3,
  input  _12,
  input  _4,
  input  _11,
  input  _5,
  input  _7_GND,
  input  _8,
  output _10,
  output _6,
  output _9
);

  or or_1 (_6, _5, _4, _3);
  or or_2 (_10, _13, _12, _11);
  or or_3 (_9, _1, _2, _8);
endmodule
