// Logisim project lab-1.circ as structural Verilog: 3 circuits, main circuit Exp-01
module Exp_01 (
  input  A,
  input  B
);

  wire ic7400_nand_1__3, ic7402_nor_1__1, ic7404_not_1_p2, ic7408_and_1__3, ic7432_or_1__3, ic7486_x_or_1__6;

  // IC7404__NOT ic7404_not_1: pin names not known; wires that end beside it: A, ic7404_not_1_p2
  DotMatrix #(.matrixcols(8), .matrixrows(1), .dotshape("circle")) dotmatrix_1 (
    .col0(ic7404_not_1_p2), .col1(ic7432_or_1__3), .col2(ic7408_and_1__3), .col3(ic7400_nand_1__3),
    .col4(ic7402_nor_1__1), .col5(ic7486_x_or_1__6));  // open: col6, col7
  IC7432__OR ic7432_or_1 (
    ._1(B), ._2(A), ._3(ic7432_or_1__3));  // open: _4, _5, _6, _7_GND, _14_VCC, _13, _12, _11, _10, _9, _8
  IC7408__AND ic7408_and_1 (
    ._1(A), ._2(B), ._3(ic7408_and_1__3));  // open: _4, _5, _6, _7_GND, _14_VCC, _13, _12, _11, _10, _9, _8
  IC7400__NAND ic7400_nand_1 (
    ._1(A), ._2(B), ._3(ic7400_nand_1__3));  // open: _4, _5, _6, _7_GND, _14_VCC, _13, _12, _11, _10, _9, _8
  IC7402__NOR ic7402_nor_1 (
    ._1(ic7402_nor_1__1), ._2(A), ._3(B));  // open: _4, _5, _6, _7_GND, _14_VCC, _13, _12, _11, _10, _9, _8
  IC7486__X_OR ic7486_x_or_1 (
    ._4(A), ._5(B), ._6(ic7486_x_or_1__6));  // open: _1, _2, _3, _7_GND, _14_VCC, _13, _12, _11, _10, _9, _8

  // Notes on the sheet:
  //   Introduction to Basic Logic Gate
endmodule

module Exp_02 (
  input  A,
  input  B,
  input  C,
  output out_4,
  output out_5
);

  wire ic7408_and_1__11, ic7432_or_1__3;

  IC7432__OR ic7432_or_1 (
    ._1(A), ._2(B), ._3(ic7432_or_1__3), ._4(ic7432_or_1__3), ._5(C), ._6(out_4));  // open: _7_GND, _14_VCC, _13, _12, _11, _10, _9, _8
  IC7408__AND ic7408_and_1 (
    ._13(A), ._12(B), ._11(ic7408_and_1__11), ._10(ic7408_and_1__11), ._9(C), ._8(out_5));  // open: _1, _2, _3, _4, _5, _6, _7_GND, _14_VCC

  // Notes on the sheet:
  //   3 input AND & OR Gates Using 2 input AND & OR Gates
endmodule

module Exp_03 (
  input  A,
  input  B,
  input  C,
  output out_4
);

  wire ic7404_not_1_p2, ic7404_not_1_p4, ic7408_and_1__3, ic7408_and_1__6, ic7408_and_1__8, ic7432_or_1__3;

  // IC7404__NOT ic7404_not_1: pin names not known; wires that end beside it: A, ic7404_not_1_p2, B, ic7404_not_1_p4
  IC7408__AND ic7408_and_1 (
    ._1(ic7404_not_1_p2), ._2(C), ._3(ic7408_and_1__3), ._4(B), ._5(C), ._6(ic7408_and_1__6), ._10(A),
    ._9(ic7404_not_1_p4), ._8(ic7408_and_1__8));  // open: _7_GND, _14_VCC, _13, _12, _11
  IC7432__OR ic7432_or_1 (
    ._1(ic7408_and_1__8), ._2(ic7408_and_1__6), ._3(ic7432_or_1__3), ._4(ic7432_or_1__3),
    ._5(ic7408_and_1__3), ._6(out_4));  // open: _7_GND, _14_VCC, _13, _12, _11, _10, _9, _8

  // Notes on the sheet:
  //   Implenention of boolean function F=A'C+AB'+BC
endmodule
