// Logisim project lab-2.circ as structural Verilog: 2 circuits, main circuit 2nd canonical (POS)
module _2nd_canonical__POS (
  input  A,
  input  B,
  input  C,
  output F
);

  wire not_1_out, not_2_out, not_3_out, not_4_out, not_5_out, not_6_out, or_1_out, or_2_out, or_3_out,
       or_4_out, or_5_out;

  not not_1 (not_1_out, B);
  not not_2 (not_2_out, C);
  not not_3 (not_3_out, A);
  not not_4 (not_4_out, C);
  not not_5 (not_5_out, B);
  not not_6 (not_6_out, A);
  or or_1 (or_1_out, A, B, C);
  or or_2 (or_2_out, A, not_1_out, not_2_out);
  or or_3 (or_3_out, not_3_out, B, not_4_out);
  or or_4 (or_4_out, not_3_out, B, C);
  or or_5 (or_5_out, C, not_5_out, not_6_out);
  and and_1 (F, or_1_out, or_2_out, or_3_out, or_4_out, or_5_out);
endmodule

module _1st_canonical (
  input  A,
  input  B,
  input  C,
  output F
);

  wire ic7411_and_3_1__6, ic7411_and_3_1__12, NOT_p2, NOT_p4, NOT_p6;

  // IC7404__NOT NOT: pin names not known; wires that end beside it: A, NOT_p2, B, NOT_p4, C, NOT_p6, 1'b0, 1'b1
  IC7411__AND_3 ic7411_and_3_1 (
    ._1(NOT_p2), ._2(NOT_p4), ._3(B), ._4(NOT_p6), ._5(1'b1), ._6(ic7411_and_3_1__6), ._7_GND(1'b0),
    ._14_VCC(1'b1), ._13(C), ._12(ic7411_and_3_1__12));  // open: _11, _10, _9, _8
  IC7432__OR ic7432_or_1 (
    ._1(ic7411_and_3_1__12), ._2(ic7411_and_3_1__6), ._3(F), ._7_GND(1'b0), ._14_VCC(1'b1));  // open: _4, _5, _6, _13, _12, _11, _10, _9, _8

  // Notes on the sheet:
  //   F=A'B'C+BC' 
endmodule
