// Logisim project lab-3.circ as structural Verilog
module main (
  input  in_1,
  input  in_2,
  input  in_3,
  output out_4
);

  wire and_1_out, and_2_out, not_1_out;

  not not_1 (not_1_out, in_3);
  and and_1 (and_1_out, in_1, in_3);
  and and_2 (and_2_out, in_2, not_1_out);
  or or_1 (out_4, and_1_out, and_2_out);
endmodule

module \nor  (
  input  A,
  input  B,
  input  C,
  output F
);

  wire nor_1_out, nor_2_out, nor_3_out, nor_4_out, nor_5_out, nor_6_out;

  nor nor_1 (nor_1_out, A, A);
  nor nor_2 (nor_2_out, C, C);
  nor nor_3 (nor_3_out, B, B);
  nor nor_4 (nor_4_out, nor_1_out, nor_2_out);
  nor nor_5 (nor_5_out, nor_3_out, C);
  nor nor_6 (nor_6_out, nor_4_out, nor_5_out);
  nor nor_7 (F, nor_6_out, nor_6_out);

  // Notes on the sheet:
  //   F=AC+BC'
endmodule

module XOR (
  input  A,
  input  B,
  output out_3
);

  wire nand_1_out, nand_2_out, nand_3_out, nand_4_out;

  nand nand_1 (nand_1_out, A, B);
  nand nand_2 (nand_2_out, A, nand_1_out);
  nand nand_3 (nand_3_out, nand_1_out, B);
  nand nand_4 (nand_4_out, nand_2_out, nand_3_out);
  nand nand_5 (out_3, nand_4_out, nand_4_out);
endmodule

module basic_gates (
  input  A,
  input  B,
  input  C,
  output F
);

  wire and_1_out, and_2_out, not_1_out;

  and and_1 (and_1_out, A, C);
  and and_2 (and_2_out, B, not_1_out);
  not not_1 (not_1_out, C);
  or or_1 (F, and_1_out, and_2_out);
endmodule

module NAND (
  input  A,
  input  B,
  input  C,
  output out_4
);

  wire nand_1_out, nand_2_out, nand_3_out;

  nand nand_1 (nand_1_out, C, C);
  nand nand_2 (nand_2_out, A, C);
  nand nand_3 (nand_3_out, B, nand_1_out);
  nand nand_4 (out_4, nand_2_out, nand_3_out);
endmodule

module ic (
  input  A,
  input  B,
  input  C
);

  wire ic7400_nand_1__3;

  IC7400__NAND ic7400_nand_1 (
    ._1(A), ._2(C), ._3(ic7400_nand_1__3), ._7_GND(1'b0), ._14_VCC(1'b1), ._13(ic7400_nand_1__3));  // open: _4, _5, _6, _12, _11, _10, _9, _8
endmodule
