// Logisim project lab-4.circ as structural Verilog
module group (
  input  W,
  input  X,
  input  Y,
  input  Z,
  output A,
  output B,
  output C,
  output D
);

  wire and_1_out, and_2_out, and_3_out, and_4_out, and_5_out, and_6_out, and_7_out, not_1_out, not_2_out,
       not_3_out;

  not not_1 (not_1_out, W);
  not not_2 (not_2_out, X);
  not not_3 (not_3_out, Y);
  not not_4 (D, Z);
  and and_1 (and_1_out, X, Z);
  and and_2 (and_2_out, X, Y);
  and and_3 (and_3_out, not_2_out, Z);
  and and_4 (and_4_out, not_2_out, Y);
  and and_5 (and_5_out, X, not_3_out, D);
  and and_6 (and_6_out, Y, Z);
  and and_7 (and_7_out, not_3_out, D);
  or or_1 (A, W, and_1_out, and_2_out);
  or or_2 (B, and_3_out, and_4_out, and_5_out);
  or or_3 (C, and_6_out, and_7_out);
endmodule

module NOR (
  input  W,
  input  X,
  input  Y,
  input  Z,
  output A,
  output B,
  output C,
  output D
);

  wire nor_1_out, nor_2_out, nor_3_out, nor_4_out, nor_5_out, nor_6_out, nor_7_out, nor_8_out, nor_9_out,
       nor_10_out, nor_11_out, nor_12_out, nor_13_out, nor_16_out, nor_17_out;

  nor nor_1 (nor_1_out, X, X);
  nor nor_2 (nor_2_out, Y, Z);
  nor nor_3 (nor_3_out, Y, Z);
  nor nor_4 (nor_4_out, Y, Y);
  nor nor_5 (nor_5_out, Z, Z);
  nor nor_6 (nor_6_out, nor_1_out, nor_2_out);
  nor nor_7 (nor_7_out, X, nor_3_out);
  nor nor_8 (nor_8_out, nor_3_out, nor_3_out);
  nor nor_9 (nor_9_out, X, X);
  nor nor_10 (nor_10_out, Y, Z);
  nor nor_11 (nor_11_out, nor_10_out, nor_12_out);
  nor nor_12 (nor_12_out, nor_4_out, nor_5_out);
  nor nor_13 (nor_13_out, nor_8_out, nor_9_out);
  nor nor_14 (C, nor_11_out, nor_11_out);
  nor nor_15 (D, Z, Z);
  nor nor_16 (nor_16_out, nor_6_out, W);
  nor nor_17 (nor_17_out, nor_7_out, nor_13_out);
  nor nor_18 (A, nor_16_out, nor_16_out);
  nor nor_19 (B, nor_17_out, nor_17_out);
endmodule

module Riad (
  input  W,
  input  X,
  input  Y,
  input  Z,
  output A,
  output B,
  output C,
  output D
);

  wire nand_1_out, nand_2_out, nand_3_out, nand_4_out, nand_5_out, nand_6_out, nand_7_out, nand_9_out,
       nand_10_out, nand_11_out, nand_12_out, nand_13_out, nand_14_out, nand_15_out, nand_16_out,
       nand_17_out, nand_18_out, nand_19_out, nand_22_out, nand_23_out;

  nand nand_1 (nand_1_out, X, Z);
  nand nand_2 (nand_2_out, X, Y);
  nand nand_3 (nand_3_out, X, X);
  nand nand_4 (nand_4_out, X, X);
  nand nand_5 (nand_5_out, Y, Y);
  nand nand_6 (nand_6_out, Y, Y);
  nand nand_7 (nand_7_out, Z, Z);
  nand nand_8 (D, Z, Z);
  nand nand_9 (nand_9_out, nand_1_out, nand_2_out);
  nand nand_10 (nand_10_out, nand_3_out, Z);
  nand nand_11 (nand_11_out, nand_4_out, Y);
  nand nand_12 (nand_12_out, X, nand_5_out);
  nand nand_13 (nand_13_out, nand_6_out, nand_7_out);
  nand nand_14 (nand_14_out, Y, Z);
  nand nand_15 (nand_15_out, nand_9_out, nand_9_out);
  nand nand_16 (nand_16_out, W, W);
  nand nand_17 (nand_17_out, nand_10_out, nand_11_out);
  nand nand_18 (nand_18_out, nand_12_out, nand_12_out);
  nand nand_19 (nand_19_out, Z, Z);
  nand nand_20 (C, nand_13_out, nand_14_out);
  nand nand_21 (A, nand_15_out, nand_16_out);
  nand nand_22 (nand_22_out, nand_17_out, nand_17_out);
  nand nand_23 (nand_23_out, nand_18_out, nand_19_out);
  nand nand_24 (B, nand_22_out, nand_23_out);
endmodule

module test (
  input  W,
  input  X,
  input  Y,
  input  Z,
  output A,
  output B,
  output C,
  output D
);

  wire nand_1_out, nand_2_out, nand_3_out, nand_4_out, nand_5_out, nand_6_out, nand_7_out, nand_9_out,
       nand_10_out, nand_11_out, nand_12_out, nand_13_out, nand_14_out, nand_15_out, nand_16_out,
       nand_17_out, nand_18_out, nand_19_out, nand_22_out, nand_23_out;

  nand nand_1 (nand_1_out, X, Z);
  nand nand_2 (nand_2_out, X, Y);
  nand nand_3 (nand_3_out, X, X);
  nand nand_4 (nand_4_out, X, X);
  nand nand_5 (nand_5_out, Y, Y);
  nand nand_6 (nand_6_out, Y, Y);
  nand nand_7 (nand_7_out, Z, Z);
  nand nand_8 (D, Z, Z);
  nand nand_9 (nand_9_out, nand_1_out, nand_2_out);
  nand nand_10 (nand_10_out, nand_3_out, Z);
  nand nand_11 (nand_11_out, nand_4_out, Y);
  nand nand_12 (nand_12_out, X, nand_5_out);
  nand nand_13 (nand_13_out, nand_6_out, nand_7_out);
  nand nand_14 (nand_14_out, Y, Z);
  nand nand_15 (nand_15_out, nand_9_out, nand_9_out);
  nand nand_16 (nand_16_out, W, W);
  nand nand_17 (nand_17_out, nand_10_out, nand_11_out);
  nand nand_18 (nand_18_out, nand_12_out, nand_12_out);
  nand nand_19 (nand_19_out, Z, Z);
  nand nand_20 (C, nand_13_out, nand_14_out);
  nand nand_21 (A, nand_15_out, nand_16_out);
  nand nand_22 (nand_22_out, nand_17_out, nand_17_out);
  nand nand_23 (nand_23_out, nand_18_out, nand_19_out);
  nand nand_24 (B, nand_22_out, nand_23_out);
endmodule

module Abir (
  input  W,
  input  X,
  input  Y,
  input  Z,
  output A,
  output B,
  output C,
  output D
);

  wire nand_1_out, nand_2_out, nand_3_out, nand_4_out, nand_5_out, nand_6_out, nand_7_out, nand_8_out,
       nand_9_out, nand_12_out, nand_13_out, nand_14_out, nand_15_out, nand_16_out;

  nand nand_1 (nand_1_out, X, Z);
  nand nand_2 (nand_2_out, X, Y);
  nand nand_3 (nand_3_out, W, W);
  nand nand_4 (nand_4_out, X, X);
  nand nand_5 (nand_5_out, X, X);
  nand nand_6 (nand_6_out, Y, Y);
  nand nand_7 (nand_7_out, Z, Z);
  nand nand_8 (nand_8_out, Y, Y);
  nand nand_9 (nand_9_out, Z, Z);
  nand nand_10 (D, Z, Z);
  nand nand_11 (A, nand_1_out, nand_2_out, nand_3_out);
  nand nand_12 (nand_12_out, nand_4_out, Z);
  nand nand_13 (nand_13_out, nand_5_out, Y);
  nand nand_14 (nand_14_out, X, nand_6_out, nand_7_out);
  nand nand_15 (nand_15_out, nand_8_out, nand_9_out);
  nand nand_16 (nand_16_out, Y, Z);
  nand nand_17 (B, nand_12_out, nand_13_out, nand_14_out);
  nand nand_18 (C, nand_15_out, nand_16_out);
endmodule
