// Logisim project lab-5.circ as structural Verilog: 4 circuits, main circuit main
module main (
  input  A4,
  input  A3,
  input  A2,
  input  A1,
  input  B4,
  input  B3,
  input  B2,
  input  B1,
  input  M,
  output S4,
  output S3,
  output S2,
  output S1,
  output C_out
);

  wire xor_1_out, xor_2_out, xor_3_out, xor_4_out;

  xor xor_1 (xor_1_out, B4, M);
  xor xor_2 (xor_2_out, B3, M);
  xor xor_3 (xor_3_out, B2, M);
  xor xor_4 (xor_4_out, B1, M);
  // IC_74283 ic_74283_1: pin names not known; wires that end beside it: A4, A3, A2, A1, xor_1_out, xor_2_out, xor_3_out, xor_4_out, M, S4, S3, S2, S1, C_out
endmodule

module Adder (
  input  A4,
  input  A3,
  input  A2,
  input  A1,
  input  B4,
  input  B3,
  input  B2,
  input  B1,
  output Carry_bit,
  output S4,
  output S3,
  output S2,
  output S1
);

  wire and_1_out, and_2_out, and_3_out, and_4_out, and_5_out, and_6_out, and_7_out, and_8_out, or_2_out,
       or_3_out, or_4_out, xor_1_out, xor_3_out, xor_5_out, xor_7_out;

  or or_1 (Carry_bit, and_1_out, and_2_out);
  and and_1 (and_1_out, A4, B4);
  and and_2 (and_2_out, xor_1_out, or_2_out);
  xor xor_1 (xor_1_out, B4, A4);
  or or_2 (or_2_out, and_3_out, and_4_out);
  xor xor_2 (S4, or_2_out, xor_1_out);
  and and_3 (and_3_out, A3, B3);
  and and_4 (and_4_out, xor_3_out, or_3_out);
  xor xor_3 (xor_3_out, B3, A3);
  or or_3 (or_3_out, and_5_out, and_6_out);
  xor xor_4 (S3, or_3_out, xor_3_out);
  xor xor_5 (xor_5_out, B2, A2);
  and and_5 (and_5_out, A2, B2);
  xor xor_6 (S2, or_4_out, xor_5_out);
  and and_6 (and_6_out, xor_5_out, or_4_out);
  or or_4 (or_4_out, and_7_out, and_8_out);
  xor xor_7 (xor_7_out, B1, A1);
  and and_7 (and_7_out, A1, B1);
  and and_8 (and_8_out, xor_7_out, 1'b0);
  xor xor_8 (S1, 1'b0, xor_7_out);

  // Notes on the sheet:
  //   4-bit Adder
  //   Group - 09 (Binary equivalence - 1001)
  //   (10010)_2 = (18)_10
endmodule

module Adder_subtructor (
  input  A4,
  input  A3,
  input  A2,
  input  A1,
  input  B4,
  input  B3,
  input  B2,
  input  B1,
  input  M,
  output S4,
  output S3,
  output S2,
  output S1,
  output C_out
);

  wire xor_1_out, xor_2_out, xor_3_out, xor_4_out;

  xor xor_1 (xor_1_out, B4, M);
  xor xor_2 (xor_2_out, B3, M);
  xor xor_3 (xor_3_out, B2, M);
  xor xor_4 (xor_4_out, B1, M);
  // IC_74283 ic_74283_1: pin names not known; wires that end beside it: A4, A3, A2, A1, xor_1_out, xor_2_out, xor_3_out, xor_4_out, M, S4, S3, S2, S1, C_out

  // Notes on the sheet:
  //   Adder-Subtructor
endmodule

module bcd_adder (
  input  in_1,
  input  in_2,
  input  in_3,
  input  in_4,
  input  in_5,
  input  in_6,
  input  in_7,
  input  in_8,
  output out_9,
  output out_10,
  output out_11,
  output out_12,
  output out_13
);

  wire and_1_out, and_2_out, ic_74283_1_p2, ic_74283_1_p8, ic_74283_1_p10, ic_74283_1_p12, ic_74283_1_p14,
       or_2_out;

  or or_1 (out_9, ic_74283_1_p2, or_2_out);
  and and_1 (and_1_out, ic_74283_1_p8, ic_74283_1_p10);
  or or_2 (or_2_out, and_1_out, and_2_out);
  and and_2 (and_2_out, ic_74283_1_p12, ic_74283_1_p8);
  // IC_74283 ic_74283_1: pin names not known; wires that end beside it: 1'b0, ic_74283_1_p2, in_1, in_2, in_3, in_4, in_5, ic_74283_1_p8, in_6, ic_74283_1_p10, in_7, ic_74283_1_p12, in_8, ic_74283_1_p14
  // IC_74283 ic_74283_2: pin names not known; wires that end beside it: 1'b0, 1'b0, out_9, out_9, 1'b0, ic_74283_1_p8, out_10, ic_74283_1_p10, out_11, ic_74283_1_p12, out_12, ic_74283_1_p14, out_13
endmodule
