// Logisim project lab-6.circ as structural Verilog: 2 circuits, main circuit main
module main (
  input  A,
  input  B,
  input  C,
  input  in_4,
  input  C_2,
  input  B_2,
  input  A_2,
  input  in_8,
  input  in_9,
  input  in_10,
  input  in_11,
  input  in_12,
  input  in_13,
  input  in_14,
  output Y0,
  output Y1,
  output Y2,
  output Y3,
  output Y4,
  output Y5,
  output Y6,
  output Y7,
  output out_23,
  output out_24
);

  // IC_74151 ic_74151_1: pin names not known; wires that end beside it: in_4, in_8, in_9, in_10, in_11, in_12, in_13, in_14, C, B, 1'b0, A, out_23, out_24
  // IC_74138 ic_74138_1: pin names not known; wires that end beside it: Y0, Y1, Y2, Y3, A_2, Y4, B_2, Y5, C_2, Y6, Y7, 1'b1, 1'b0, 1'b0

  // Notes on the sheet:
  //   Riad Safowan - 2112312642
  //   8:1 MUX
  //   Riad Safowan - 2112312642
  //   3 to 8 Line Decoder
endmodule

module abir (
  input  A,
  input  B,
  input  C,
  input  A_2,
  input  B_2,
  input  C_2,
  input  in_7,
  input  in_8,
  input  in_9,
  input  in_10,
  input  in_11,
  input  in_12,
  input  in_13,
  input  in_14,
  output Y0,
  output Y1,
  output Y2,
  output Y3,
  output Y4,
  output Y5,
  output Y6,
  output Y7,
  output out_23,
  output out_24
);

  // IC_74151 ic_74151_1: pin names not known; wires that end beside it: A_2, B_2, C_2, in_7, in_8, in_9, out_23, in_10, in_11, in_12, in_13, out_24, in_14, 1'b0
  // IC_74138 ic_74138_1: pin names not known; wires that end beside it: A, B, C, 1'b0, 1'b0, 1'b1, Y0, Y1, Y2, Y3, Y4, Y5, Y6, Y7, Y7
endmodule
