// Logisim project lab-7 7 segment display.circ as structural Verilog: 1 circuit, main circuit main
module main (
  input  D,
  input  C,
  input  B,
  input  A,
  input  _0,
  input  _1,
  input  _2,
  input  _3,
  input  _4,
  input  _5,
  input  _6,
  input  _7,
  input  _8,
  input  _9,
  input  X,
  input  X_2,
  input  X_3,
  input  X_4,
  input  X_5,
  input  X_6,
  input  in_21,
  input  in_22,
  input  in_23
);

  wire a_out, and_1_out, and_2_out, and_3_out, and_4_out, and_5_out, and_6_out, and_7_out, and_8_out,
       and_9_out, and_10_out, and_11_out, and_12_out, b_out, c_out, d_out, e_out, f_out, g_out, not_1_out,
       not_2_out, not_3_out, not_4_out, xnor_1_out, xor_1_out;
  wire [2:0] clock_1_out;
  wire [3:0] multiplexer_1_out, priority_encoder_1_out;

  Priority_Encoder #(.select(4)) priority_encoder_1 (
    .in0(_0), .in1(_1), .in2(_2), .in3(_3), .in4(_4), .in5(_5), .in6(_6), .in7(_7), .in8(_8), .in9(_9),
    .in10(X), .in11(X_2), .in12(X_3), .in13(X_4), .in14(X_5), .in15(X_6), .out(priority_encoder_1_out));  // open: gs, en_out, en_in
  Clock clock_1 (.out(clock_1_out[0]));
  Clock #(.highDuration(2), .lowDuration(2)) clock_2 (.out(clock_1_out[1]));
  Clock #(.highDuration(4), .lowDuration(4)) clock_3 (.out(clock_1_out[2]));
  Multiplexer #(.select(2), .width(4)) multiplexer_1 (
    .in0({D, C, B, A}), .in1(priority_encoder_1_out), .in2({in_21, clock_1_out}), .in3({in_21, clock_1_out}),
    .out(multiplexer_1_out), .sel({in_22, in_23}), .en(1'b1));
  not not_1 (not_1_out, multiplexer_1_out[3]);
  not not_2 (not_2_out, multiplexer_1_out[2]);
  not not_3 (not_3_out, multiplexer_1_out[1]);
  not not_4 (not_4_out, multiplexer_1_out[0]);
  and and_1 (and_1_out, not_4_out, not_3_out, not_2_out);
  and and_2 (and_2_out, multiplexer_1_out[2], multiplexer_1_out[0]);
  and and_3 (and_3_out, multiplexer_1_out[0], not_3_out, multiplexer_1_out[2]);
  and and_4 (and_4_out, not_1_out, not_2_out, not_4_out);
  and and_5 (and_5_out, multiplexer_1_out[1], not_2_out);
  and and_6 (and_6_out, not_4_out, multiplexer_1_out[1]);
  and and_7 (and_7_out, not_4_out, not_3_out, not_2_out);
  and and_8 (and_8_out, not_4_out, multiplexer_1_out[1]);
  and and_9 (and_9_out, not_4_out, not_3_out);
  and and_10 (and_10_out, not_4_out, multiplexer_1_out[2]);
  and and_11 (and_11_out, not_3_out, multiplexer_1_out[2]);
  and and_12 (and_12_out, not_4_out, multiplexer_1_out[2]);
  xnor xnor_1 (xnor_1_out, multiplexer_1_out[0], multiplexer_1_out[1]);
  xor xor_1 (xor_1_out, multiplexer_1_out[2], multiplexer_1_out[1]);
  or u_a (a_out, and_1_out, and_2_out, multiplexer_1_out[3], multiplexer_1_out[1]);
  or u_b (b_out, xnor_1_out, not_2_out);
  or u_c (c_out, not_3_out, multiplexer_1_out[0], multiplexer_1_out[2]);
  or u_d (d_out, and_3_out, and_4_out, and_5_out, and_6_out, multiplexer_1_out[3]);
  or e (e_out, and_7_out, and_8_out);
  or f (f_out, and_9_out, and_10_out, and_11_out, multiplexer_1_out[3]);
  or g (g_out, xor_1_out, and_12_out, multiplexer_1_out[3]);
  _7_Segment_Display u_7_segment_display_1 (
    .g(g_out), .f(f_out), .a(a_out), .b(b_out), .e(e_out), .d(d_out), .c(c_out), .dp(1'b1));
endmodule
