// Logisim project lab-8 flip-flop.circ as structural Verilog: 3 circuits, main circuit main
module main (
  input  in_1,
  input  in_2,
  input  in_3,
  output out_4,
  output out_5,
  output out_6,
  output out_7,
  output out_8,
  output out_9,
  output out_10,
  output out_11,
  output out_12,
  output out_13
);

  wire and_1_out, and_2_out, and_3_out, and_4_out, and_5_out, and_6_out, and_7_out, and_8_out, clock_1_out,
       clock_2_out, clock_3_out, d_ff_1_q, d_ff_2_q, d_ff_3_q, nor_2_out, nor_4_out, nor_6_out, nor_8_out,
       not_1_out, not_2_out, not_3_out, not_4_out;

  Clock clock_1 (.out(clock_1_out));
  not not_1 (not_1_out, in_1);
  Clock clock_2 (.out(clock_2_out));
  // DIP_7474 dip_7474_1: pin names not known; wires that end beside it: in_2, clock_1_out, out_8, out_8, clock_1_out, out_9
  and and_1 (and_1_out, out_4, not_1_out, clock_2_out);
  nor nor_1 (out_4, and_1_out, nor_2_out);
  nor nor_2 (nor_2_out, out_4, and_2_out);
  and and_2 (and_2_out, clock_2_out, in_1, nor_2_out);
  // DIP_7474 dip_7474_2: pin names not known; wires that end beside it: out_9, clock_1_out, out_10, out_10, clock_1_out, out_11
  and and_3 (and_3_out, out_5, not_2_out, clock_2_out);
  not not_2 (not_2_out, out_4);
  and and_4 (and_4_out, clock_2_out, out_4, nor_4_out);
  nor nor_3 (out_5, and_3_out, nor_4_out);
  nor nor_4 (nor_4_out, out_5, and_4_out);
  not not_3 (not_3_out, out_5);
  Clock clock_3 (.out(clock_3_out));
  and and_5 (and_5_out, out_6, not_3_out, clock_2_out);
  and and_6 (and_6_out, clock_2_out, out_5, nor_6_out);
  D_Flip_Flop d_ff_1 (.clk(clock_3_out), .D(in_3), .Q(d_ff_1_q));  // open: Qn, preset, en, reset
  nor nor_5 (out_6, and_5_out, nor_6_out);
  nor nor_6 (nor_6_out, out_6, and_6_out);
  D_Flip_Flop d_ff_2 (.clk(clock_3_out), .D(d_ff_1_q), .Q(d_ff_2_q));  // open: Qn, preset, en, reset
  D_Flip_Flop d_ff_3 (.clk(clock_3_out), .D(d_ff_2_q), .Q(d_ff_3_q));  // open: Qn, preset, en, reset
  not not_4 (not_4_out, out_6);
  D_Flip_Flop d_ff_4 (.clk(clock_3_out), .D(d_ff_3_q), .Q(out_13));  // open: Qn, preset, en, reset
  and and_7 (and_7_out, out_7, not_4_out, clock_2_out);
  and and_8 (and_8_out, clock_2_out, out_6, nor_8_out);
  nor nor_7 (out_7, and_7_out, nor_8_out);
  nor nor_8 (nor_8_out, out_7, and_8_out);

  assign out_12 = out_11;
endmodule

module combinational (
  input  A4,
  input  A3,
  input  A2,
  input  A1,
  input  in_5,
  input  in_6,
  input  in_7,
  input  in_8,
  input  in_9,
  input  in_10,
  input  in_11,
  input  in_12,
  input  in_13,
  input  in_14,
  input  in_15,
  input  in_16,
  input  in_17,
  input  in_18,
  input  in_19
);

  wire a_2_out, a_out, and_1_out, and_2_out, and_3_out, and_4_out, and_5_out, and_6_out, and_7_out,
       and_8_out, and_11_out, and_12_out, and_15_out, and_16_out, and_17_out, and_18_out, and_19_out,
       and_20_out, and_21_out, and_22_out, and_23_out, and_24_out, and_25_out, and_26_out, and_27_out,
       and_28_out, and_29_out, and_30_out, and_31_out, and_32_out, and_33_out, and_34_out, and_35_out,
       and_36_out, and_37_out, and_38_out, and_39_out, and_40_out, and_41_out, and_42_out, and_43_out,
       and_44_out, and_45_out, and_46_out, and_47_out, and_48_out, and_49_out, and_50_out, and_51_out,
       and_52_out, and_53_out, and_54_out, and_55_out, and_56_out, and_57_out, and_58_out, and_59_out,
       and_60_out, and_61_out, b_2_out, b_out, c_2_out, c_out, clock_1_out, d_2_out, d_ff_1_q, d_ff_2_q,
       d_ff_3_q, d_ff_4_q, d_ff_5_q, d_ff_6_q, d_ff_7_q, d_ff_8_q, d_out, e_2_out, e_out, f_2_out, f_out,
       g_2_out, g_out, not_1_out, not_2_out, not_3_out, not_4_out, not_5_out, not_6_out, not_7_out,
       not_8_out, not_9_out, not_10_out, or_3_out, or_4_out, or_5_out, or_6_out, or_7_out, or_8_out,
       or_9_out, or_10_out, or_11_out, or_12_out, or_13_out, or_14_out, or_15_out, or_16_out, or_17_out,
       or_18_out, or_19_out, or_20_out, or_21_out, or_22_out, or_23_out, priority_encoder_1_p5,
       priority_encoder_1_p6, priority_encoder_1_p7, xnor_1_out, xnor_2_out, xor_1_out, xor_2_out, xor_3_out,
       xor_5_out, xor_6_out, xor_7_out, xor_9_out, xor_10_out, xor_11_out, xor_13_out, xor_14_out,
       xor_15_out, xor_16_out, xor_17_out, xor_19_out, xor_20_out, xor_21_out, xor_23_out, xor_24_out,
       xor_25_out, xor_27_out, xor_28_out, xor_29_out, xor_31_out, xor_32_out, xor_33_out;
  wire [1:0] priority_encoder_1_p3;
  wire [3:0] priority_encoder_2_p1, xor_18_out, xor_34_out;
  wire [7:0] and_10_out, multiplexer_1_out;
  wire [7:7] priority_encoder_1_p4;

  // OR_Gate or_1 has open pins: in0=and_1_out, in1=and_2_out, out=open
  // OR_Gate or_2 has open pins: in0=and_3_out, in1=and_4_out, out=open
  and and_1 (and_1_out, A4, d_ff_1_q);
  xor xor_1 (xor_1_out, d_ff_1_q, A4);
  xor xor_2 (xor_2_out, or_3_out, xor_1_out);
  and and_2 (and_2_out, xor_1_out, or_3_out);
  // Priority_Encoder #(.select(2)) priority_encoder_1: pin names not known; wires that end beside it: 1'b0, 1'b1, priority_encoder_1_p3, priority_encoder_1_p4[7], priority_encoder_1_p5, priority_encoder_1_p6, priority_encoder_1_p7
  and and_3 (and_3_out, xor_2_out, and_10_out[7]);
  and and_4 (and_4_out, xor_3_out, or_4_out);
  or or_3 (or_3_out, and_5_out, and_6_out);
  xor xor_3 (xor_3_out, and_10_out[7], xor_2_out);
  or or_4 (or_4_out, and_7_out, and_8_out);
  xor xor_4 (xor_18_out[3], or_4_out, xor_3_out);
  not not_1 (not_1_out, xor_18_out[2]);
  not not_2 (not_2_out, xor_18_out[3]);
  not not_3 (not_3_out, xor_34_out[2]);
  not not_4 (not_4_out, xor_34_out[3]);
  xor xor_5 (xor_5_out, d_ff_2_q, A3);
  and and_5 (and_5_out, A3, d_ff_2_q);
  xor xor_6 (xor_6_out, or_5_out, xor_5_out);
  and and_6 (and_6_out, xor_5_out, or_5_out);
  xor xor_7 (xor_7_out, and_10_out[6], xor_6_out);
  and and_7 (and_7_out, xor_6_out, and_10_out[6]);
  xor xor_8 (xor_18_out[2], or_6_out, xor_7_out);
  and and_8 (and_8_out, xor_7_out, or_6_out);
  not not_5 (not_5_out, xor_18_out[1]);
  not not_6 (not_6_out, xor_34_out[1]);
  or or_5 (or_5_out, and_11_out, and_12_out);
  and and_9 (priority_encoder_1_p5, or_7_out, or_9_out);
  Multiplexer #(.select(2), .width(8)) multiplexer_1 (
    .in0(8'h6), .in1(8'hc), .in2(8'h12), .in3(8'h30), .out(multiplexer_1_out), .sel(priority_encoder_1_p3));  // open: en
  assign and_10_out = multiplexer_1_out & {8{priority_encoder_1_p4[7]}};  // AND_Gate and_10, 8 bits wide
  or or_6 (or_6_out, and_15_out, and_16_out);
  not not_7 (not_7_out, xor_18_out[0]);
  not not_8 (not_8_out, xor_34_out[0]);
  buf xor_9 (xor_9_out, d_ff_3_q);  // XOR_Gate
  and and_11 (and_11_out, A2, d_ff_3_q);
  and and_12 (and_12_out, xor_9_out, or_8_out);
  xor xor_10 (xor_10_out, or_8_out, xor_9_out);
  or or_7 (or_7_out, xor_6_out, xor_10_out, xor_16_out, not_9_out, xor_24_out, xor_28_out);
  and and_13 (priority_encoder_1_p6, or_10_out, or_11_out);
  and and_14 (priority_encoder_1_p7, or_12_out, or_13_out, or_14_out);
  xor xor_11 (xor_11_out, and_10_out[5], xor_10_out);
  and and_15 (and_15_out, xor_10_out, and_10_out[5]);
  and and_16 (and_16_out, xor_11_out, or_15_out);
  xor xor_12 (xor_18_out[1], or_15_out, xor_11_out);
  and and_17 (and_17_out, not_7_out, not_5_out, not_1_out);
  and and_18 (and_18_out, xor_18_out[2], xor_18_out[0]);
  xnor xnor_1 (xnor_1_out, xor_18_out[0], xor_18_out[1]);
  and and_19 (and_19_out, xor_18_out[0], not_5_out, xor_18_out[2]);
  and and_20 (and_20_out, not_2_out, not_1_out, not_7_out);
  and and_21 (and_21_out, xor_18_out[1], not_1_out);
  and and_22 (and_22_out, not_7_out, xor_18_out[1]);
  and and_23 (and_23_out, not_7_out, not_5_out, not_1_out);
  and and_24 (and_24_out, not_7_out, xor_18_out[1]);
  and and_25 (and_25_out, not_7_out, not_5_out);
  and and_26 (and_26_out, not_7_out, xor_18_out[2]);
  and and_27 (and_27_out, not_5_out, xor_18_out[2]);
  xor xor_13 (xor_13_out, xor_18_out[2], xor_18_out[1]);
  and and_28 (and_28_out, not_7_out, xor_18_out[2]);
  and and_29 (and_29_out, not_8_out, not_6_out, not_3_out);
  and and_30 (and_30_out, xor_34_out[2], xor_34_out[0]);
  xnor xnor_2 (xnor_2_out, xor_34_out[0], xor_34_out[1]);
  and and_31 (and_31_out, xor_34_out[0], not_6_out, xor_34_out[2]);
  and and_32 (and_32_out, not_4_out, not_3_out, not_8_out);
  and and_33 (and_33_out, xor_34_out[1], not_3_out);
  and and_34 (and_34_out, not_8_out, xor_34_out[1]);
  and and_35 (and_35_out, not_8_out, not_6_out, not_3_out);
  and and_36 (and_36_out, not_8_out, xor_34_out[1]);
  and and_37 (and_37_out, not_8_out, not_6_out);
  and and_38 (and_38_out, not_8_out, xor_34_out[2]);
  and and_39 (and_39_out, not_6_out, xor_34_out[2]);
  xor xor_14 (xor_14_out, xor_34_out[2], xor_34_out[1]);
  and and_40 (and_40_out, not_8_out, xor_34_out[2]);
  D_Flip_Flop d_ff_1 (.clk(clock_1_out), .D(xor_2_out), .Q(d_ff_1_q));  // open: Qn, preset, en, reset
  or or_8 (or_8_out, and_41_out, and_42_out);
  not not_9 (not_9_out, xor_20_out);
  or or_9 (or_9_out, xor_6_out, xor_10_out, xor_16_out, xor_20_out);
  or or_10 (or_10_out, xor_6_out, xor_10_out, xor_16_out);
  or or_11 (or_11_out, xor_6_out, xor_10_out, xor_20_out, xor_24_out);
  or or_12 (or_12_out, xor_6_out, xor_16_out, xor_10_out);
  or or_13 (or_13_out, xor_6_out, xor_10_out, xor_20_out);
  or or_14 (or_14_out, xor_6_out, xor_10_out, and_51_out, not_10_out);
  or or_15 (or_15_out, and_43_out, and_44_out);
  D_Flip_Flop d_ff_2 (.clk(clock_1_out), .D(xor_6_out), .Q(d_ff_2_q));  // open: Qn, preset, en, reset
  xor xor_15 (xor_15_out, d_ff_4_q, A1);
  and and_41 (and_41_out, A1, d_ff_4_q);
  and and_42 (and_42_out, xor_15_out, or_16_out);
  xor xor_16 (xor_16_out, or_16_out, xor_15_out);
  xor xor_17 (xor_17_out, and_10_out[4], xor_16_out);
  and and_43 (and_43_out, xor_16_out, and_10_out[4]);
  xor xor_18 (xor_18_out[0], or_17_out, xor_17_out);
  and and_44 (and_44_out, xor_17_out, or_17_out);
  or a (a_out, and_17_out, and_18_out, xor_18_out[3], xor_18_out[1]);
  or b (b_out, xnor_1_out, not_1_out);
  or c (c_out, not_5_out, xor_18_out[0], xor_18_out[2]);
  or d (d_out, and_19_out, and_20_out, and_21_out, and_22_out, xor_18_out[3]);
  or e (e_out, and_23_out, and_24_out);
  or f (f_out, and_25_out, and_26_out, and_27_out, xor_18_out[3]);
  or g (g_out, xor_13_out, and_28_out, xor_18_out[3]);
  or a_2 (a_2_out, and_29_out, and_30_out, xor_34_out[3], xor_34_out[1]);
  or b_2 (b_2_out, xnor_2_out, not_3_out);
  or c_2 (c_2_out, not_6_out, xor_34_out[0], xor_34_out[2]);
  or d_2 (d_2_out, and_31_out, and_32_out, and_33_out, and_34_out, xor_34_out[3]);
  or e_2 (e_2_out, and_35_out, and_36_out);
  or f_2 (f_2_out, and_37_out, and_38_out, and_39_out, xor_34_out[3]);
  or g_2 (g_2_out, xor_14_out, and_40_out, xor_34_out[3]);
  D_Flip_Flop d_ff_3 (.clk(clock_1_out), .D(xor_10_out), .Q(d_ff_3_q));  // open: Qn, preset, en, reset
  or or_16 (or_16_out, and_45_out, and_46_out);
  not not_10 (not_10_out, xor_20_out);
  or or_17 (or_17_out, and_47_out, and_48_out);
  D_Flip_Flop d_ff_4 (.clk(clock_1_out), .D(xor_16_out), .Q(d_ff_4_q));  // open: Qn, preset, en, reset
  and and_45 (and_45_out, priority_encoder_2_p1[3], d_ff_5_q);
  xor xor_19 (xor_19_out, d_ff_5_q, priority_encoder_2_p1[3]);
  xor xor_20 (xor_20_out, or_18_out, xor_19_out);
  and and_46 (and_46_out, xor_19_out, or_18_out);
  xor xor_21 (xor_21_out, and_10_out[3], xor_20_out);
  and and_47 (and_47_out, xor_20_out, and_10_out[3]);
  xor xor_22 (xor_34_out[3], or_19_out, xor_21_out);
  and and_48 (and_48_out, xor_21_out, or_19_out);
  Clock clock_1 (.out(clock_1_out));
  D_Flip_Flop d_ff_5 (.clk(clock_1_out), .D(xor_20_out), .Q(d_ff_5_q));  // open: Qn, preset, en, reset
  and and_49 (and_49_out, priority_encoder_2_p1[2], d_ff_6_q);
  or or_18 (or_18_out, and_49_out, and_50_out);
  and and_50 (and_50_out, xor_23_out, or_20_out);
  and and_51 (and_51_out, xor_24_out, xor_28_out);
  or or_19 (or_19_out, and_52_out, and_53_out);
  D_Flip_Flop d_ff_6 (.clk(clock_1_out), .D(xor_24_out), .Q(d_ff_6_q));  // open: Qn, preset, en, reset
  xor xor_23 (xor_23_out, d_ff_6_q, priority_encoder_2_p1[2]);
  xor xor_24 (xor_24_out, or_20_out, xor_23_out);
  and and_52 (and_52_out, xor_24_out, and_10_out[2]);
  xor xor_25 (xor_25_out, and_10_out[2], xor_24_out);
  and and_53 (and_53_out, xor_25_out, or_21_out);
  xor xor_26 (xor_34_out[2], or_21_out, xor_25_out);
  D_Flip_Flop d_ff_7 (.clk(clock_1_out), .D(xor_28_out), .Q(d_ff_7_q));  // open: Qn, preset, en, reset
  and and_54 (and_54_out, priority_encoder_2_p1[1], d_ff_7_q);
  or or_20 (or_20_out, and_54_out, and_55_out);
  and and_55 (and_55_out, xor_27_out, or_22_out);
  and and_56 (and_56_out, xor_28_out, and_10_out[1]);
  or or_21 (or_21_out, and_56_out, and_57_out);
  and and_57 (and_57_out, xor_29_out, or_23_out);
  D_Flip_Flop d_ff_8 (.clk(clock_1_out), .D(xor_32_out), .Q(d_ff_8_q));  // open: Qn, preset, en, reset
  xor xor_27 (xor_27_out, d_ff_7_q, priority_encoder_2_p1[1]);
  or or_22 (or_22_out, and_58_out, and_59_out);
  xor xor_28 (xor_28_out, or_22_out, xor_27_out);
  xor xor_29 (xor_29_out, and_10_out[1], xor_28_out);
  xor xor_30 (xor_34_out[1], or_23_out, xor_29_out);
  and and_58 (and_58_out, priority_encoder_2_p1[0], d_ff_8_q);
  and and_59 (and_59_out, xor_31_out, 1'b0);
  and and_60 (and_60_out, xor_32_out, and_10_out[0]);
  or or_23 (or_23_out, and_60_out, and_61_out);
  and and_61 (and_61_out, xor_33_out, 1'b0);
  xor xor_31 (xor_31_out, d_ff_8_q, priority_encoder_2_p1[0]);
  xor xor_32 (xor_32_out, 1'b0, xor_31_out);
  xor xor_33 (xor_33_out, and_10_out[0], xor_32_out);
  xor xor_34 (xor_34_out[0], 1'b0, xor_33_out);
  _7_Segment_Display u_7_segment_display_1 (
    .g(g_out), .f(f_out), .a(a_out), .b(b_out), .e(e_out), .d(d_out), .c(c_out), .dp(1'b0));
  // Priority_Encoder #(.select(4)) priority_encoder_2: pin names not known; wires that end beside it: priority_encoder_2_p1, 1'b1, in_5, in_6, in_7, in_8, in_9, in_10, in_11, in_12, in_13, in_14, in_15, in_16, in_17, in_18, in_19
  _7_Segment_Display u_7_segment_display_2 (
    .g(g_2_out), .f(f_2_out), .a(a_2_out), .b(b_2_out), .e(e_2_out), .d(d_2_out), .c(c_2_out), .dp(1'b0));
endmodule

module combination_2 (
  input  in_1,
  input  in_2,
  input  in_3,
  input  in_4,
  input  in_5,
  input  in_6,
  input  in_7,
  input  in_8,
  output Carry_bit,
  output S1,
  output S4,
  output S3,
  output S2,
  output S1_2
);

  wire a_2_out, a_out, and_1_out, and_2_out, and_3_out, and_4_out, and_5_out, and_6_out, and_7_out,
       and_8_out, and_9_out, and_10_out, and_11_out, and_12_out, and_13_out, and_14_out, and_15_out,
       and_16_out, and_17_out, and_18_out, and_19_out, and_20_out, and_21_out, and_22_out, and_23_out,
       and_24_out, and_25_out, and_26_out, and_27_out, and_28_out, and_29_out, and_30_out, and_31_out,
       and_32_out, and_33_out, and_34_out, and_35_out, and_36_out, and_37_out, and_38_out, and_39_out,
       and_40_out, and_41_out, and_42_out, and_43_out, and_44_out, and_46_out, and_47_out, b_2_out, b_out,
       c_2_out, c_out, clock_1_out, d_2_out, d_ff_1_q, d_ff_2_q, d_ff_3_q, d_ff_4_q, d_ff_5_q, d_out,
       e_2_out, e_out, f_2_out, f_out, g_2_out, g_out, not_1_out, not_2_out, not_3_out, not_4_out, not_5_out,
       not_6_out, not_7_out, not_8_out, not_9_out, or_3_out, or_4_out, or_5_out, or_6_out, or_7_out,
       or_8_out, or_9_out, or_10_out, or_11_out, or_12_out, or_13_out, priority_encoder_2_out, xnor_1_out,
       xnor_2_out, xor_1_out, xor_2_out, xor_3_out, xor_5_out, xor_7_out, xor_9_out, xor_11_out, xor_13_out,
       xor_15_out, xor_17_out, xor_19_out, xor_21_out;
  wire [1:0] xor_4_out;
  wire [2:0] priority_encoder_1_out;
  wire [3:0] xor_20_out;
  wire [4:0] and_45_out, multiplexer_1_out;
  wire [4:4] priority_encoder_2_gs;

  not not_1 (not_1_out, 1'b0);
  not not_2 (not_2_out, 1'b0);
  not not_3 (not_3_out, xor_20_out[3]);
  not not_4 (not_4_out, xor_20_out[2]);
  not not_5 (not_5_out, xor_4_out[1]);
  not not_6 (not_6_out, xor_4_out[0]);
  not not_7 (not_7_out, xor_20_out[1]);
  not not_8 (not_8_out, xor_20_out[0]);
  and and_1 (and_1_out, not_6_out, not_5_out, not_2_out);
  and and_2 (and_2_out, 1'b0, xor_4_out[0]);
  xnor xnor_1 (xnor_1_out, xor_4_out[0], xor_4_out[1]);
  and and_3 (and_3_out, xor_4_out[0], not_5_out, 1'b0);
  and and_4 (and_4_out, not_1_out, not_2_out, not_6_out);
  and and_5 (and_5_out, xor_4_out[1], not_2_out);
  and and_6 (and_6_out, not_6_out, xor_4_out[1]);
  and and_7 (and_7_out, not_6_out, not_5_out, not_2_out);
  and and_8 (and_8_out, not_6_out, xor_4_out[1]);
  and and_9 (and_9_out, not_6_out, not_5_out);
  and and_10 (and_10_out, not_6_out, 1'b0);
  and and_11 (and_11_out, not_5_out, 1'b0);
  xor xor_1 (xor_1_out, 1'b0, xor_4_out[1]);
  and and_12 (and_12_out, not_6_out, 1'b0);
  and and_13 (and_13_out, not_8_out, not_7_out, not_4_out);
  and and_14 (and_14_out, xor_20_out[2], xor_20_out[0]);
  xnor xnor_2 (xnor_2_out, xor_20_out[0], xor_20_out[1]);
  and and_15 (and_15_out, xor_20_out[0], not_7_out, xor_20_out[2]);
  and and_16 (and_16_out, not_3_out, not_4_out, not_8_out);
  and and_17 (and_17_out, xor_20_out[1], not_4_out);
  and and_18 (and_18_out, not_8_out, xor_20_out[1]);
  and and_19 (and_19_out, not_8_out, not_7_out, not_4_out);
  and and_20 (and_20_out, not_8_out, xor_20_out[1]);
  and and_21 (and_21_out, not_8_out, not_7_out);
  and and_22 (and_22_out, not_8_out, xor_20_out[2]);
  and and_23 (and_23_out, not_7_out, xor_20_out[2]);
  xor xor_2 (xor_2_out, xor_20_out[2], xor_20_out[1]);
  and and_24 (and_24_out, not_8_out, xor_20_out[2]);
  or a (a_out, and_1_out, and_2_out, 1'b0, xor_4_out[1]);
  or b (b_out, xnor_1_out, not_2_out);
  or c (c_out, not_5_out, xor_4_out[0], 1'b0);
  or d (d_out, and_3_out, and_4_out, and_5_out, and_6_out, 1'b0);
  or e (e_out, and_7_out, and_8_out);
  or f (f_out, and_9_out, and_10_out, and_11_out, 1'b0);
  or g (g_out, xor_1_out, and_12_out, 1'b0);
  or a_2 (a_2_out, and_13_out, and_14_out, xor_20_out[3], xor_20_out[1]);
  or b_2 (b_2_out, xnor_2_out, not_4_out);
  or c_2 (c_2_out, not_7_out, xor_20_out[0], xor_20_out[2]);
  or d_2 (d_2_out, and_15_out, and_16_out, and_17_out, and_18_out, xor_20_out[3]);
  or e_2 (e_2_out, and_19_out, and_20_out);
  or f_2 (f_2_out, and_21_out, and_22_out, and_23_out, xor_20_out[3]);
  or g_2 (g_2_out, xor_2_out, and_24_out, xor_20_out[3]);
  _7_Segment_Display u_7_segment_display_1 (
    .g(g_out), .f(f_out), .a(a_out), .b(b_out), .e(e_out), .d(d_out), .c(c_out), .dp(1'b1));
  _7_Segment_Display u_7_segment_display_2 (
    .g(g_2_out), .f(f_2_out), .a(a_2_out), .b(b_2_out), .e(e_2_out), .d(d_2_out), .c(c_2_out), .dp(1'b1));
  Priority_Encoder priority_encoder_1 (
    .in0(in_1), .in1(in_2), .in2(in_3), .in3(in_4), .in4(in_5), .in5(in_6), .in6(in_7), .in7(in_8),
    .out(priority_encoder_1_out));  // open: en_in, gs, en_out
  or or_1 (xor_4_out[1], and_27_out, and_28_out);
  and and_25 (and_25_out, 1'b0, d_ff_1_q);
  or or_2 (Carry_bit, and_25_out, and_26_out);
  and and_26 (and_26_out, xor_5_out, or_4_out);
  xor xor_3 (xor_3_out, and_45_out[4], S1);
  and and_27 (and_27_out, S1, and_45_out[4]);
  xor xor_4 (xor_4_out[0], or_3_out, xor_3_out);
  and and_28 (and_28_out, xor_3_out, or_3_out);
  xor xor_5 (xor_5_out, d_ff_1_q, 1'b0);
  xor xor_6 (S1, or_4_out, xor_5_out);
  or or_3 (or_3_out, and_31_out, and_32_out);
  and and_29 (and_29_out, 1'b0, d_ff_2_q);
  or or_4 (or_4_out, and_29_out, and_30_out);
  and and_30 (and_30_out, xor_9_out, or_6_out);
  xor xor_7 (xor_7_out, and_45_out[3], S4);
  and and_31 (and_31_out, S4, and_45_out[3]);
  xor xor_8 (xor_20_out[3], or_5_out, xor_7_out);
  and and_32 (and_32_out, xor_7_out, or_5_out);
  Clock clock_1 (.out(clock_1_out));
  D_Flip_Flop d_ff_1 (.clk(clock_1_out), .D(S1), .Q(d_ff_1_q));  // open: Qn, preset, en, reset
  xor xor_9 (xor_9_out, d_ff_2_q, 1'b0);
  xor xor_10 (S4, or_6_out, xor_9_out);
  or or_5 (or_5_out, and_35_out, and_36_out);
  D_Flip_Flop d_ff_2 (.clk(clock_1_out), .D(S4), .Q(d_ff_2_q));  // open: Qn, preset, en, reset
  and and_33 (and_33_out, priority_encoder_1_out[0], d_ff_3_q);
  or or_6 (or_6_out, and_33_out, and_34_out);
  and and_34 (and_34_out, xor_13_out, or_7_out);
  xor xor_11 (xor_11_out, and_45_out[2], S3);
  and and_35 (and_35_out, S3, and_45_out[2]);
  xor xor_12 (xor_20_out[2], or_8_out, xor_11_out);
  and and_36 (and_36_out, xor_11_out, or_8_out);
  D_Flip_Flop d_ff_3 (.clk(clock_1_out), .D(S3), .Q(d_ff_3_q));  // open: Qn, preset, en, reset
  xor xor_13 (xor_13_out, d_ff_3_q, priority_encoder_1_out[0]);
  or or_7 (or_7_out, and_37_out, and_38_out);
  xor xor_14 (S3, or_7_out, xor_13_out);
  not not_9 (not_9_out, S1);
  or or_8 (or_8_out, and_39_out, and_40_out);
  D_Flip_Flop d_ff_4 (.clk(clock_1_out), .D(S2), .Q(d_ff_4_q));  // open: Qn, preset, en, reset
  and and_37 (and_37_out, priority_encoder_1_out[1], d_ff_4_q);
  and and_38 (and_38_out, xor_17_out, or_11_out);
  or or_9 (or_9_out, S2, S3);
  or or_10 (or_10_out, S3, S4);
  xor xor_15 (xor_15_out, and_45_out[1], S2);
  and and_39 (and_39_out, S2, and_45_out[1]);
  xor xor_16 (xor_20_out[1], or_12_out, xor_15_out);
  and and_40 (and_40_out, xor_15_out, or_12_out);
  D_Flip_Flop d_ff_5 (.clk(clock_1_out), .D(S1_2), .Q(d_ff_5_q));  // open: Qn, preset, en, reset
  xor xor_17 (xor_17_out, d_ff_4_q, priority_encoder_1_out[1]);
  or or_11 (or_11_out, and_43_out, and_44_out);
  xor xor_18 (S2, or_11_out, xor_17_out);
  and and_41 (and_41_out, or_9_out, S4, not_9_out);
  and and_42 (and_42_out, or_10_out, S1);
  or or_12 (or_12_out, and_46_out, and_47_out);
  and and_43 (and_43_out, priority_encoder_1_out[2], d_ff_5_q);
  and and_44 (and_44_out, xor_21_out, 1'b0);
  or or_13 (or_13_out, and_41_out, S1);
  assign and_45_out = {5{priority_encoder_2_gs[4]}} & multiplexer_1_out;  // AND_Gate and_45, 5 bits wide
  and and_46 (and_46_out, S1_2, and_45_out[0]);
  xor xor_19 (xor_19_out, and_45_out[0], S1_2);
  xor xor_20 (xor_20_out[0], 1'b0, xor_19_out);
  and and_47 (and_47_out, xor_19_out, 1'b0);
  xor xor_21 (xor_21_out, d_ff_5_q, priority_encoder_1_out[2]);
  xor xor_22 (S1_2, 1'b0, xor_21_out);
  Priority_Encoder #(.select(1)) priority_encoder_2 (
    .in0(or_13_out), .in1(and_42_out), .out(priority_encoder_2_out), .gs(priority_encoder_2_gs[4]));  // open: en_out, en_in
  Multiplexer #(.width(5)) multiplexer_1 (
    .in0(5'b00110), .in1(5'b01100), .out(multiplexer_1_out), .sel(priority_encoder_2_out));  // open: en
endmodule
